# Fritzing sketch power supply (saved by Fritzing 0.9.6b)
breadboards: 1

parts:
  HLK-PM1 = HLK-PM01  # not connected
  M1 = TP4056 Module [part_number=HW-107]
  J1 = Camdenboss CTB0158-2 [part_number=CTB0158-2 package=THT]
  BAT1 = 18650 battery holder [package=battery-18650-kit]
  U2 = Mini-360 DC-DC Buck converter [package=THT]

nets:
  N1: M1.pin3, BAT1.-
  N2: M1.pin4, BAT1.+
  N3: J1.pin2, U2.OUT+

custom parts:
  TP4056 Module: TP4056 Lithium Battery Charge Management Module Links: TP4056 website
  18650 battery holder: 18650 Battery Holder
  Mini-360 DC-DC Buck converter: Mini-360 DC-DC Buck converter. Tiny buck step down voltage converter, input voltage 4.75 to 23V output 1 to 17V adjustable. Available from ebay and the like.
