# Fritzing sketch sketch-ESP32_With_ETH-20250308 (saved by Fritzing 1.0.1rc)
breadboards: 1

parts:
  ZS-042_RTC1 = ZS-042 RTC Module
  Squix1 = OLED 0.96" 128x64 I2C SSD1306
  LED1 = LED - 5mm [color="Red (633nm)" current=0.030 package="5 mm [THT]"]
  LED2 = LED - 5mm [color="Green (555nm)" current=0.030 package="5 mm [THT]"]
  LED3 = LED - 5mm [color="Yellow (595nm)" current=0.030 package="5 mm [THT]"]
  R2 = Resistor [tolerance=±5% resistance=220 package="2512 [SMD]"]
  S1 = Pushbutton [package="[SMD]"]
  R3 = Resistor [tolerance=±5% resistance=220 package="0402 [SMD]"]
  R4 = Resistor [tolerance=±5% resistance=220 package="0402 [SMD]"]
  A2 = GT-U8-GPS module
  M1 = >Wemos D1 R32
  A3 = w5500 module

nets:
  N1: ZS-042_RTC1.SDA, Squix1.SCA
  N2: ZS-042_RTC1.SCL, Squix1.SCL
  VCC: Squix1.VCC, A2.Pin_1, M1.3V3, A3.Pin_10, A3.Pin_11
  GND: Squix1.GND, LED1.cathode, LED2.cathode, LED3.cathode, S1.Pin_1, S1.Pin_2, A2.Pin_2, M1.GND, A3.Pin_2, A3.Pin_12
  N3: LED1.anode, R2.Pin_1
  N4: LED2.anode, R3.Pin_1
  N5: LED3.anode, R4.Pin_1
  N6: R2.Pin_0, M1.IO27
  N7: S1.Pin_3, S1.Pin_4, M1.IO26
  N8: R3.Pin_0, M1.IO13, A3.Pin_8
  N9: R4.Pin_0, M1.IO14
  N10: A2.Pin_3, M1.IO16
  N11: A2.Pin_4, M1.IO17
  N12: A2.Pin_5, M1.IO12
  N13: M1.IO25, A3.Pin_6
  N14: M1.IO5, A3.Pin_5
  N15: M1.IO23, A3.Pin_3
  N16: M1.IO19, A3.Pin_7
  N17: M1.IO18, A3.Pin_4

notes:
  SDA - IO21
  SCL - IO22
  GNSS Time Server
  ESP32 Ethernet Version Wiring Diagram
  cristianomonteiro@gmail.com
  https://github.com/Montecri/GNSSTimeServer

custom parts:
  GT-U8-GPS module: GPS / BDS W/GT-U8 WITH CERAMIC ANTENNA.
  >Wemos D1 R32: Wemos D1 R32 - This board is used with dual-mode Wi-Fi and Bluetooth chips, which is safe, reliable, and scalable to a variety of applications. DC in 5V-12V, 1 analog input(3.2V max input), a Micro USB connection, Compatible with D1 R32=WiFi+bluetooth+UNO
  w5500 module: MELIFE 3pcs W5500 SPI to LAN Ethernet Network Module TCP IP STM32 Interface 3.3V 5V Compatible with WIZ820io RC5.
