# Fritzing sketch sketch-ESP32_Without_ETH-20250308 (saved by Fritzing 1.0.1rc)
breadboards: 1

parts:
  ZS-042_RTC1 = ZS-042 RTC Module
  Squix1 = OLED 0.96" 128x64 I2C SSD1306
  LED1 = LED - 5mm [color="Red (633nm)" current=0.030 package="5 mm [THT]"]
  LED2 = LED - 5mm [color="Green (555nm)" current=0.030 package="5 mm [THT]"]
  LED3 = LED - 5mm [color="Yellow (595nm)" current=0.030 package="5 mm [THT]"]
  R2 = Resistor [tolerance=±5% resistance=220 package="2512 [SMD]"]
  S1 = Pushbutton [package="[SMD]"]
  R3 = Resistor [tolerance=±5% resistance=220 package="0402 [SMD]"]
  R4 = Resistor [tolerance=±5% resistance=220 package="0402 [SMD]"]
  A2 = GT-U8-GPS module
  M1 = >Wemos D1 R32

nets:
  N1: ZS-042_RTC1.SDA, Squix1.SCA
  N2: ZS-042_RTC1.SCL, Squix1.SCL
  VCC: Squix1.VCC, A2.Pin_1, M1.3V3
  GND: Squix1.GND, LED1.cathode, LED2.cathode, LED3.cathode, S1.Pin_1, S1.Pin_2, A2.Pin_2, M1.GND
  N3: LED1.anode, R2.Pin_1
  N4: LED2.anode, R3.Pin_1
  N5: LED3.anode, R4.Pin_1
  N6: R2.Pin_0, M1.IO27
  N7: S1.Pin_3, S1.Pin_4, M1.IO5
  N8: R3.Pin_0, M1.IO19
  N9: R4.Pin_0, M1.IO14
  N10: A2.Pin_3, M1.IO16
  N11: A2.Pin_4, M1.IO17
  N12: A2.Pin_5, M1.IO12

notes:
  SDA - IO21
  SCL - IO22
  GNSS Time Server
  ESP32 Wiring Diagram
  cristianomonteiro@gmail.com
  https://github.com/Montecri/GNSSTimeServer

custom parts:
  GT-U8-GPS module: GPS / BDS W/GT-U8 WITH CERAMIC ANTENNA.
  >Wemos D1 R32: Wemos D1 R32 - This board is used with dual-mode Wi-Fi and Bluetooth chips, which is safe, reliable, and scalable to a variety of applications. DC in 5V-12V, 1 analog input(3.2V max input), a Micro USB connection, Compatible with D1 R32=WiFi+bluetooth+UNO
