# Fritzing sketch sketch (saved by Fritzing 0.9.6b)
breadboards: 1

parts:
  Amica_NodeMCU_DevKit_1_1 = Amica NodeMCU DevKit 1.0
  ZS-042_RTC1 = ZS-042 RTC Module
  Squix1 = OLED 0.96" 128x64 I2C SSD1306
  Part1 = u-blox NEO-6M GPS Breakout
  LED1 = LED - 5mm [color="Red (633nm)" current=0.030 package="5 mm [THT]"]
  LED2 = LED - 5mm [color="Green (555nm)" current=0.030 package="5 mm [THT]"]
  LED3 = LED - 5mm [color="Yellow (595nm)" current=0.030 package="5 mm [THT]"]
  R2 = Resistor [tolerance=±5% resistance=220 package="2512 [SMD]"]
  S1 = Pushbutton [package="[SMD]"]
  R3 = Resistor [tolerance=±5% resistance=220 package="0402 [SMD]"]
  R4 = Resistor [tolerance=±5% resistance=220 package="0402 [SMD]"]

nets:
  VCC: Amica_NodeMCU_DevKit_1_1.pin1, Amica_NodeMCU_DevKit_1_1.pin_10, Amica_NodeMCU_DevKit_1_1.pin_26, Squix1.VCC, Part1.VCC
  GND: Amica_NodeMCU_DevKit_1_1.pin2, Amica_NodeMCU_DevKit_1_1.pin_9, Amica_NodeMCU_DevKit_1_1.pin_25, Amica_NodeMCU_DevKit_1_1.pin_29, Squix1.GND, Part1.GND, LED1.cathode, LED2.cathode, LED3.cathode, S1.Pin_1, S1.Pin_2
  N1: Amica_NodeMCU_DevKit_1_1.pin5, Part1.RXD
  N2: Amica_NodeMCU_DevKit_1_1.pin6, Part1.TXD
  N3: Amica_NodeMCU_DevKit_1_1.pin7, Part1.PPS
  N4: Amica_NodeMCU_DevKit_1_1.pin8, R4.Pin_0
  N5: Amica_NodeMCU_DevKit_1_1.pin_11, S1.Pin_3, S1.Pin_4
  N6: Amica_NodeMCU_DevKit_1_1.pin_12, R3.Pin_0
  N7: Amica_NodeMCU_DevKit_1_1.pin_19, R2.Pin_0
  N8: ZS-042_RTC1.SDA, Squix1.SCA
  N9: ZS-042_RTC1.SCL, Squix1.SCL
  N10: LED1.anode, R2.Pin_1
  N11: LED2.anode, R3.Pin_1
  N12: LED3.anode, R4.Pin_1

custom parts:
  Amica NodeMCU DevKit 1.0: Amica NodeMCU DEVKIT 1.0 Development Kit based on ESP8266 ESP-12E, integating GPIO, PWM, IIC, 1-Wire and ADC all in one board.
